# Fritzing sketch LED Standard (saved by Fritzing 0.8.5b)
breadboards: 1

parts:
  R3 = Resistor [tolerance=±5% resistance=330 package=THT]
  LED1 = LED - 5mm [color="White (4500K)" package="5 mm [THT]"]
  Part1 = Arduino Uno (Rev3)

nets:
  N1: R3.Pin_0, LED1.anode
  N2: R3.Pin_1, Part1.D3_PWM
  N3: LED1.cathode, Part1.GND

notes:
  LED ~3.3V Forward Voltage
  LED IF=20mA
  Ardiono ~5V Output (except for 3.3V pin)
  V=IR, Resistor = (5V-3.3V) / IF(20mA / 1000) ohm
  Minimum Resistor Size: 85ohm
  Common Resistor Size: 100ohm
