# Fritzing sketch RGB LED Common Anode (saved by Fritzing 0.8.5b)
breadboards: 1

parts:
  Part1 = Arduino Uno (Rev3)
  LED1 = RGB LED (com. cathode, rgb) [package="5 mm [THT]"]
  R3 = Resistor [tolerance=±5% resistance=330 package=THT]

nets (from the breadboard view):
  N1: Part1.D9_PWM, LED1.blue_anode
  N2: Part1.D10_PWM/SS, LED1.green_anode
  N3: Part1.D11_PWM/MOSI, LED1.red_anode
  N4: LED1.common_cathode, R3.Pin_1

notes:
  RGB LED ~2V Forward Voltage
  LED IF=20mA
  Ardiono ~5V Output (except for 3.3V pin)
  V=IR, Resistor = (5V-2V) / IF(20mA / 1000) ohm
  Minimum Resistor Size: 150ohm
  Common Resistor Size: 200ohm
