# Fritzing sketch RGB LED Common Cathode (saved by Fritzing 0.8.5b)
breadboards: 1

parts:
  Part1 = Arduino Uno (Rev3)
  R1 = Resistor [tolerance=±5% resistance=330 package=THT]
  R2 = Resistor [tolerance=±5% resistance=330 package=THT]
  R3 = Resistor [tolerance=±5% resistance=330 package=THT]
  LED1 = RGB LED (com. cathode, rgb) [package="5 mm [THT]"]

nets:
  N1: Part1.D9_PWM, R1.Pin_1
  N2: Part1.D10_PWM/SS, R2.Pin_1
  N3: Part1.D11_PWM/MOSI, R3.Pin_1
  N4: Part1.GND, LED1.common_cathode
  N5: R1.Pin_0, LED1.blue_anode
  N6: R2.Pin_0, LED1.green_anode
  N7: R3.Pin_0, LED1.red_anode

notes:
  RGB LED ~2V Forward Voltage
  LED IF=20mA
  Ardiono ~5V Output (except for 3.3V pin)
  V=IR, Resistor = (5V-2V) / IF(20mA / 1000) ohm
  Minimum Resistor Size: 150ohm
  Common Resistor Size: 200ohm
