# Fritzing sketch Buttons_Code_Example (saved by Fritzing 0.8.5b)
breadboards: 1

parts:
  Arduino = Arduino Uno (Rev3)
  Switch = Pushbutton [package="[SMD]"]
  R1 = Resistor [tolerance=±5% resistance=10k package=THT]
  Toggle = Toggle Switch [package=THT]
  R2 = Resistor [tolerance=±5% resistance=10k package=THT]
  LED1 = LED - 5mm [color="Green (555nm)" package="5 mm [THT]"]
  R3 = Resistor [tolerance=±5% resistance=330 package=THT]
  Trimpot = Trimmer Potentiometer [maximum_resistance=10kΩ package=THT]

nets:
  N1: Arduino.A0, Trimpot.wiper
  N2: Arduino.D9_PWM, R3.Pin_0
  N3: Arduino.D3_PWM, Toggle.L2, R2.Pin_0
  N4: Arduino.D4, Switch.Pin_3, Switch.Pin_4, R1.Pin_0
  N5: Arduino.5V, Switch.Pin_1, Switch.Pin_2, Toggle.COM, Trimpot.leg1
  N6: Arduino.GND, R1.Pin_1, R2.Pin_1, LED1.cathode, Trimpot.leg2
  N7: LED1.anode, R3.Pin_1
