# Fritzing sketch Buttons_NoCode_Example (saved by Fritzing 0.8.5b)
breadboards: 2

parts:
  Part1 = Arduino Uno (Rev3)
  S1 = Momentary Switch [package=ksa_sealed_tac_switch]
  R1 = TRIMPOT [package=trimpot_pth_s3_lock]
  U1 = SWITCH_SPDT [package=kps-1290]
  R2 = Resistor [tolerance=±5% resistance=330 package=THT]
  R3 = Resistor [tolerance=±5% resistance=330 package=THT]
  R4 = Resistor [tolerance=±5% resistance=330 package=THT]
  LED1 = LED - 3mm [color="Green (555nm)" package="3 mm [THT]"]
  LED2 = LED - 3mm [color="Green (555nm)" package="3 mm [THT]"]
  LED3 = LED - 3mm [color="Green (555nm)" package="3 mm [THT]"]
  VCC1 = Battery
  S2 = Momentary Switch [package=ksa_sealed_tac_switch]
  R5 = TRIMPOT [package=trimpot_pth_s3_lock]
  U2 = SWITCH_SPDT [package=kps-1290]
  R6 = Resistor [tolerance=±5% resistance=100 package=THT]
  R7 = Resistor [tolerance=±5% resistance=100 package=THT]
  R8 = Resistor [tolerance=±5% resistance=100 package=THT]
  LED4 = LED - 3mm [color="Green (555nm)" package="3 mm [THT]"]
  LED5 = LED - 3mm [color="Green (555nm)" package="3 mm [THT]"]
  LED6 = LED - 3mm [color="Green (555nm)" package="3 mm [THT]"]

nets:
  N1: Part1.GND, R1.CW, LED1.anode, LED2.anode, LED3.anode
  N2: Part1.5V, S1.3, R1.CCW, U1.O
  N3: S1.2, R2.Pin_0
  N4: R1.WIPER, R4.Pin_0
  N5: U1.P, R3.Pin_0
  N6: R2.Pin_1, LED1.cathode
  N7: R3.Pin_1, LED2.cathode
  N8: R4.Pin_1, LED3.cathode
  N9: VCC1.-, R5.CW, LED4.anode, LED5.anode, LED6.anode
  N10: VCC1.+, S2.3, R5.CCW, U2.O
  N11: S2.2, R6.Pin_0
  N12: R5.WIPER, R8.Pin_0
  N13: U2.P, R7.Pin_0
  N14: R6.Pin_1, LED5.cathode
  N15: R7.Pin_1, LED4.cathode
  N16: R8.Pin_1, LED6.cathode
